# Fritzing sketch Rasprinter (saved by Fritzing 0.9.3b)
perfboards: 1

parts:
  USBTTL1 = Micro USB B Plug  # not connected
  USBTTL2 = USB A Plug  # not connected
  X1 = USB Connectors [package=usb-b-smt]  # not connected
  Raspberry_Pi1 = Raspberry Pi 2
  RY1 = SSR-40VA
  Mod1 = generic-ac-power-supply [package=THT]
  Grove1 = Grove OLED 128x96
  Mod2 = KY-016 RGB Full Color LED Module [package="Breakout board"]
  BMP280_Breakout1 = BMP280 Breakout Board [part_number=BMP280]
  Part1 = Si7021
  Part2 = Si7021
  IC1 = Rasberry Pi NIOR Camera [chip_label=IC package="DIP (Dual Inline) [THT]"]  # not connected
  Q1 = NPN-Transistor [package="TO92 [THT]"]
  R1 = Resistor [tolerance=±5% resistance=10k package="1206 [SMD]"]
  R2 = Resistor [tolerance=±5% resistance=10k package="1206 [SMD]"]

nets:
  3V3: Raspberry_Pi1.3v3, Grove1.VCC
  N1: Raspberry_Pi1.GPIO2, Grove1.SDA, BMP280_Breakout1.SDA, Part1.SDA, Part2.SDA
  N2: Raspberry_Pi1.GPIO3, Grove1.SCL, BMP280_Breakout1.SCL, Part1.SCL, Part2.SCL
  GND: Raspberry_Pi1.GND, Raspberry_Pi1.GPIO13, Grove1.GND, Mod2.R, Mod2.-, Part1.GND, Part2.GND, Q1.E, R2.Pin_1
  N3: Raspberry_Pi1.GPIO19, Mod2.G
  N4: Raspberry_Pi1.GPIO26, Mod2.B
  N5: Raspberry_Pi1.GPIO12, R1.Pin_0, R2.Pin_0
  N6: Raspberry_Pi1.5V, RY1.Pin_4
  N7: RY1.Pin_2, Mod1.pin2
  N8: RY1.Pin_3, Q1.C
  VCC: BMP280_Breakout1.VCC, Part1.VCC, Part2.VCC
  N9: Q1.B, R1.Pin_1

notes:
  230V AC
  MKS SGEN_L V1.0
  HOMERS TARANTULA PRO
  5V USB DC
  SHT31
  SI7021
  BMP280
  RGB Diode
  I2C SDA
  I2C SCL
  I2C +3.3V
  I2C GND
  BC337
  10k
  OLED 0,96'
  SSR-25DA

custom parts:
  SSR-40VA: SSR-40VA solid state relay.
  generic-ac-power-supply: Generic ac power supply module. Use as is, or customize the svgs to fit your particular device (as they are all different.) Provides AC input and single DC output. This is variant 2, with pcb modified to match the url for a specific device.
  KY-016 RGB Full Color LED Module: KY-016 Arduino full color 5mm RGB LED, different colors can be obtained by mixing the three primary colors.
  BMP280 Breakout Board: This is a breakout board for the Bosch Sensortec BMP280, "an absolute barometric pressure sensor especially designed for mobile applications." The operation range is 300 to 1100 hPa. Supply voltage is 1.2 to 3.6V. Operating temperature range is -40 to +85 °C.
  Si7021: Si7021 humidity and temperature sensor
  Rasberry Pi NIOR Camera: Camera
